# Fritzing sketch Arduino_Uno_sunlight_alarm_clock_v1 (saved by Fritzing 0.9.4)
breadboards: 1

parts:
  Arduino_Uno = Arduino Uno (Rev3)
  LCD = LCD screen
  LED_rot = LED - 5mm [color="Red (633nm)" package="5 mm [THT]"]
  R5 = Resistor [tolerance=±5% resistance=330 package=THT]
  Piezo = Piezo Speaker
  R1 = Resistor [tolerance=±5% resistance=10k package=THT]
  R2 = Resistor [tolerance=±5% resistance=10k package=THT]
  R3 = Resistor [tolerance=±5% resistance=10k package=THT]
  R4 = Resistor [tolerance=±5% resistance=10k package=THT]
  S1 = Pushbutton [package="[THT]"]
  S3 = Pushbutton [package="[THT]"]
  S2 = Pushbutton [package="[THT]"]
  S4 = Pushbutton [package="[THT]"]
  R7 = Rotary Potentiometer (Small) [maximum_resistance=100kΩ package=THT]
  R6 = Resistor [tolerance=±5% resistance=100 package=THT]

nets (from the schematic view):
  N1: Arduino_Uno.D8, LCD.DB7
  N2: Arduino_Uno.D9_PWM, LCD.DB6
  N3: Arduino_Uno.D10_PWM/SS, LCD.DB5
  N4: Arduino_Uno.D11_PWM/MOSI, LCD.DB4
  N5: Arduino_Uno.D12/MISO, LCD.E
  N6: Arduino_Uno.D13/SCK, LCD.RS
  GND: Arduino_Uno.GND, LCD.VSS, LCD.R/W, LCD.LED-, R5.Pin_1, Piezo.pin1, R1.Pin_1, R2.Pin_1, R3.Pin_1, R4.Pin_1, R7.wiper
  N7: Arduino_Uno.D2, R1.Pin_0, S1.Pin_1, S1.Pin_2
  N8: Arduino_Uno.D3_PWM, R2.Pin_0, S2.Pin_1, S2.Pin_2
  N9: Arduino_Uno.D4, R3.Pin_0, S3.Pin_1, S3.Pin_2
  N10: Arduino_Uno.D5_PWM, R4.Pin_0, S4.Pin_1, S4.Pin_2
  N11: Arduino_Uno.D6_PWM, LED_rot.anode
  N12: Arduino_Uno.D7, Piezo.pin2
  5V: Arduino_Uno.5V, LCD.VDD, S1.Pin_3, S1.Pin_4, S3.Pin_3, S3.Pin_4, S2.Pin_3, S2.Pin_4, S4.Pin_3, S4.Pin_4, R7.leg1, R6.Pin_0
  N13: LCD.V0, R7.leg2
  N14: LCD.LED+, R6.Pin_1
  N15: LED_rot.cathode, R5.Pin_0
